// Logisim project cpu.circ as structural Verilog: 6 circuits, main circuit main
module main (
  input  RESET
);

  wire CLK, control_unit_1_pc_write, control_unit_1_ram_addr_select, control_unit_1_ram_oe,
       control_unit_1_regs_data_mux;
  wire [1:0] control_unit_1_pc_cmd, control_unit_1_pc_isize, control_unit_1_regs_mode;
  wire [3:0] control_unit_1_regs_sela, control_unit_1_regs_selb;
  wire [15:0] bit_extender_1_out;
  wire [31:0] adder_1_out, control_unit_1_ram_offset, control_unit_1_value_out, multiplexer_1_out,
       multiplexer_2_out, PROGRAM_COUNTER_address, ram_1_data;

  Clock clock_1 (.out(CLK));
  Multiplexer #(.width(32)) multiplexer_1 (
    .in0(ram_1_data), .in1(control_unit_1_value_out), .out(multiplexer_1_out),
    .sel(control_unit_1_regs_data_mux));
  REGISTERS_ARRAY registers_array_1 (
    .DATA(multiplexer_1_out), .MODE(control_unit_1_regs_mode), .SELECT_A(control_unit_1_regs_sela),
    .SELECT_B(control_unit_1_regs_selb), .CLOCK(CLK), .RESET(RESET));  // open: OUT_A, OUT_B
  Adder #(.width(32)) adder_1 (
    .a(control_unit_1_ram_offset), .b(PROGRAM_COUNTER_address), .out(adder_1_out), .cin(1'b0));  // open: cout
  COUNTER32b PROGRAM_COUNTER (
    .JUMP_ADDRESS(control_unit_1_value_out), .INSTRUCTION_SIZE(control_unit_1_pc_isize),
    .CMD(control_unit_1_pc_cmd), .WRITE(control_unit_1_pc_write), .CLOCK(CLK), .RESET(RESET),
    .ADDRESS(PROGRAM_COUNTER_address));
  Bit_Extender #(.in_width(32), .\type ("zero")) bit_extender_1 (.in(multiplexer_2_out), .out(bit_extender_1_out));
  Multiplexer #(.width(32)) multiplexer_2 (
    .in0(adder_1_out), .in1(control_unit_1_ram_offset), .out(multiplexer_2_out),
    .sel(control_unit_1_ram_addr_select));
  RAM #(.addrWidth(16), .asyncread("true"), .dataWidth(32), .databus("bidir")) ram_1 (
    .addr(bit_extender_1_out), .oe(control_unit_1_ram_oe), .clk(CLK), .data(ram_1_data));  // open: we
  CONTROL_UNIT control_unit_1 (
    .INSTR_CONST(ram_1_data), .CLOCK(CLK), .RESET(RESET), .RAM_ADDR_SELECT(control_unit_1_ram_addr_select),
    .RAM_OE(control_unit_1_ram_oe), .RAM_OFFSET(control_unit_1_ram_offset),
    .VALUE_OUT(control_unit_1_value_out), .PC_ISIZE(control_unit_1_pc_isize), .PC_CMD(control_unit_1_pc_cmd),
    .PC_WRITE(control_unit_1_pc_write), .REGS_MODE(control_unit_1_regs_mode),
    .REGS_SELA(control_unit_1_regs_sela), .REGS_SELB(control_unit_1_regs_selb),
    .REGS_DATA_MUX(control_unit_1_regs_data_mux));
endmodule

module RAM_CONTROLLER (
  input  [31:0] WRITEIN,
  input  [20:0] ADDRESS,
  input  WRITESTART,
  input  READSTART,
  input  CLK,
  output [31:0] READOUT
);

  wire and_1_out, and_2_out, and_3_out, d_ff_1_q, d_ff_2_q, d_ff_5_q, demultiplexer_1_out0,
       demultiplexer_1_out1, demultiplexer_2_out0, demultiplexer_2_out1, demultiplexer_2_out2,
       demultiplexer_2_out3, multiplexer_1_out, not_1_out, not_2_out, or_1_out, s_r_ff_1_q, xor_1_out,
       xor_2_out, xor_3_out;
  wire [1:0] d_ff_3_q;
  wire [7:0] multiplexer_2_out, RAM1_data;
  wire [20:0] adder_1_out;

  D_Flip_Flop d_ff_1 (.D(WRITESTART), .clk(CLK), .Q(d_ff_1_q));  // open: Qn, preset, reset
  D_Flip_Flop d_ff_2 (.D(READSTART), .clk(CLK), .Q(d_ff_2_q));  // open: Qn, preset, reset
  and and_1 (and_1_out, WRITESTART, not_1_out);
  not not_1 (not_1_out, d_ff_1_q);
  and and_2 (and_2_out, READSTART, not_2_out);
  not not_2 (not_2_out, d_ff_2_q);
  or or_1 (or_1_out, and_1_out, and_2_out);
  Multiplexer multiplexer_1 (.in0(d_ff_5_q), .in1(and_2_out), .out(multiplexer_1_out), .sel(or_1_out));
  D_Flip_Flop d_ff_3 (.D(xor_1_out), .clk(CLK), .Q(d_ff_3_q[0]), .reset(xor_3_out));  // open: Qn, preset
  xor xor_1 (xor_1_out, d_ff_3_q[0], 1'b1);
  D_Flip_Flop d_ff_4 (.D(xor_2_out), .clk(CLK), .Q(d_ff_3_q[1]), .reset(xor_3_out));  // open: Qn, preset
  xor xor_2 (xor_2_out, d_ff_3_q[1], d_ff_3_q[0]);
  Adder #(.width(21)) adder_1 (.a({{19{1'b0}}, d_ff_3_q}), .b(ADDRESS), .out(adder_1_out), .cin(1'b0));  // open: cout
  S_R_Flip_Flop s_r_ff_1 (.S(or_1_out), .R(and_3_out), .clk(CLK), .Q(s_r_ff_1_q));  // open: reset, Qn, preset
  D_Flip_Flop d_ff_5 (.D(multiplexer_1_out), .clk(CLK), .Q(d_ff_5_q));  // open: Qn, preset, reset
  xor xor_3 (xor_3_out, 1'b1, s_r_ff_1_q);
  and and_3 (and_3_out, d_ff_3_q[0], d_ff_3_q[1]);
  Demultiplexer demultiplexer_1 (
    .out0(demultiplexer_1_out0), .out1(demultiplexer_1_out1), .in(s_r_ff_1_q), .sel(d_ff_5_q));
  RAM #(.addrWidth(21), .asyncread("true"), .databus("bidir")) RAM1 (
    .addr(adder_1_out), .we(demultiplexer_1_out0), .oe(demultiplexer_1_out1), .clk(CLK), .data(RAM1_data));
  Multiplexer #(.select(2), .width(8)) multiplexer_2 (
    .in0(WRITEIN[31:24]), .in1(WRITEIN[23:16]), .in2(WRITEIN[15:8]), .in3(WRITEIN[7:0]),
    .out(multiplexer_2_out), .sel(d_ff_3_q));
  assign RAM1_data = demultiplexer_1_out0 ? multiplexer_2_out : 8'bz;  // Controlled_Buffer controlled_buffer_1
  Demultiplexer #(.select(2)) demultiplexer_2 (
    .out0(demultiplexer_2_out0), .out1(demultiplexer_2_out1), .out2(demultiplexer_2_out2),
    .out3(demultiplexer_2_out3), .in(demultiplexer_1_out1), .sel(d_ff_3_q));
  Register register_1 (.D(RAM1_data), .en(demultiplexer_2_out0), .clk(CLK), .Q(READOUT[31:24]));  // open: clr
  Register register_2 (.D(RAM1_data), .en(demultiplexer_2_out1), .clk(CLK), .Q(READOUT[23:16]));  // open: clr
  Register register_3 (.D(RAM1_data), .en(demultiplexer_2_out2), .clk(CLK), .Q(READOUT[15:8]));  // open: clr
  Register register_4 (.D(RAM1_data), .en(demultiplexer_2_out3), .clk(CLK), .Q(READOUT[7:0]));  // open: clr
endmodule

module REGISTER32b (
  input  [31:0] DATA,
  input  WRITE,
  input  CLOCK,
  input  RESET,
  output [31:0] STORED
);

  Register #(.width(32)) register_1 (.D(DATA), .en(WRITE), .clk(CLOCK), .Q(STORED), .clr(RESET));
  Hex_Digit_Display hex_digit_display_1 (.value(STORED[31:28]));  // open: dp
  Hex_Digit_Display hex_digit_display_2 (.value(STORED[27:24]));  // open: dp
  Hex_Digit_Display hex_digit_display_3 (.value(STORED[23:20]));  // open: dp
  Hex_Digit_Display hex_digit_display_4 (.value(STORED[19:16]));  // open: dp
  Hex_Digit_Display hex_digit_display_5 (.value(STORED[15:12]));  // open: dp
  Hex_Digit_Display hex_digit_display_6 (.value(STORED[11:8]));  // open: dp
  Hex_Digit_Display hex_digit_display_7 (.value(STORED[7:4]));  // open: dp
  Hex_Digit_Display hex_digit_display_8 (.value(STORED[3:0]));  // open: dp
endmodule

module COUNTER32b (
  input  [31:0] JUMP_ADDRESS,
  input  [1:0] INSTRUCTION_SIZE,
  input  CLOCK,
  input  RESET,
  input  [1:0] CMD,
  input  WRITE,
  output [31:0] ADDRESS
);

  wire [31:0] adder_1_out, bit_extender_1_out, multiplexer_1_out;

  Adder #(.width(32)) adder_1 (.a(ADDRESS), .b(bit_extender_1_out), .out(adder_1_out), .cin(1'b0));  // open: cout
  assign bit_extender_1_out = {{30{1'b0}}, INSTRUCTION_SIZE};  // Bit_Extender bit_extender_1
  Multiplexer #(.select(2), .width(32)) multiplexer_1 (
    .in0(ADDRESS), .in1(adder_1_out), .in2(JUMP_ADDRESS), .in3({32{1'b0}}), .out(multiplexer_1_out), .sel(CMD));
  REGISTER32b register32b_1 (.DATA(multiplexer_1_out), .WRITE(WRITE), .CLOCK(CLOCK), .RESET(RESET), .STORED(ADDRESS));
endmodule

module CONTROL_UNIT (
  input  [31:0] INSTR_CONST,
  input  CLOCK,
  input  RESET,
  output RAM_ADDR_SELECT,
  output RAM_OE,
  output [31:0] RAM_OFFSET,
  output [31:0] VALUE_OUT,
  output [1:0] PC_ISIZE,
  output [1:0] PC_CMD,
  output PC_WRITE,
  output [1:0] REGS_MODE,
  output [3:0] REGS_SELA,
  output [3:0] REGS_SELB,
  output REGS_DATA_MUX
);

  wire and_2_out, and_3_out, FETCH, ICODE_0000, ICODE_0001, ICODE_0010, ICODE_0011, JUMP, JUMP_END,
       LOAD_CONST, LOAD_CONST_END, LOAD_RAM, LOAD_RAM_START, not_1_out, not_2_out, not_3_out, not_4_out,
       not_5_out, not_6_out, not_7_out, not_8_out, not_9_out, OPTYPE_ALU, OPTYPE_CTRLFLOW, OPTYPE_DATA,
       or_1_out, or_2_out, or_3_out, or_4_out, or_5_out, or_6_out, or_7_out, or_9_out, or_10_out, or_11_out,
       START, START_D1;
  wire [1:0] controlled_buffer_4_out, controlled_buffer_7_out;
  wire [3:0] IREG1, IREG2;
  wire [31:0] controlled_buffer_1_out, register_2_q;

  assign controlled_buffer_1_out = LOAD_RAM ? INSTR_CONST : 32'bz;  // Controlled_Buffer controlled_buffer_1
  or or_1 (or_1_out, LOAD_CONST_END, RAM_ADDR_SELECT);
  assign REGS_MODE = or_1_out ? 2'b11 : 2'bz;  // Controlled_Buffer controlled_buffer_2
  assign REGS_SELB = or_1_out ? IREG1 : 4'bz;  // Controlled_Buffer controlled_buffer_3
  or or_2 (or_2_out, LOAD_RAM, LOAD_CONST);
  assign controlled_buffer_4_out = or_2_out ? 2'b10 : 2'bz;  // Controlled_Buffer controlled_buffer_4
  or or_3 (or_3_out, LOAD_RAM_START, LOAD_CONST);
  assign controlled_buffer_1_out = or_3_out ? 32'h1 : 32'bz;  // Controlled_Buffer controlled_buffer_5
  or or_4 (or_4_out, or_3_out, LOAD_RAM);
  D_Flip_Flop u_START (.D(PC_WRITE), .clk(CLOCK), .Q(START), .preset(RESET), .reset(1'b0));  // open: Qn
  D_Flip_Flop u_START_D1 (.D(START), .clk(CLOCK), .Q(START_D1), .preset(1'b0), .reset(RESET));  // open: Qn
  assign controlled_buffer_1_out = JUMP ? 32'h1 : 32'bz;  // Controlled_Buffer controlled_buffer_6
  or or_5 (or_5_out, JUMP, or_4_out);
  assign controlled_buffer_7_out = JUMP ? 2'b10 : 2'bz;  // Controlled_Buffer controlled_buffer_7
  assign controlled_buffer_4_out = START ? 2'b01 : 2'bz;  // Controlled_Buffer controlled_buffer_8
  or or_6 (or_6_out, START, or_2_out);
  assign controlled_buffer_7_out = START ? 2'b01 : 2'bz;  // Controlled_Buffer controlled_buffer_9
  or or_7 (or_7_out, START, JUMP);
  Register #(.width(32)) register_1 (
    .D(controlled_buffer_1_out), .en(or_5_out), .clk(CLOCK), .Q(RAM_OFFSET), .clr(or_9_out));
  Register #(.width(32)) register_2 (.D(INSTR_CONST), .en(JUMP_END), .clk(CLOCK), .Q(register_2_q), .clr(RESET));
  Register #(.width(2)) register_3 (.D(controlled_buffer_4_out), .en(or_6_out), .clk(CLOCK), .Q(PC_ISIZE), .clr(RESET));
  Register #(.width(2)) register_4 (.D(controlled_buffer_7_out), .en(or_7_out), .clk(CLOCK), .Q(PC_CMD), .clr(RESET));
  Pull_Resistor pull_resistor_1 (.node(RAM_ADDR_SELECT));
  or or_8 (RAM_OE, FETCH, RAM_ADDR_SELECT);
  Pull_Resistor pull_resistor_2 (.node(RAM_OFFSET));
  or or_9 (or_9_out, START, RESET);
  Pull_Resistor pull_resistor_3 (.node(REGS_MODE));
  Pull_Resistor pull_resistor_4 (.node(REGS_SELA));
  Pull_Resistor pull_resistor_5 (.node(REGS_SELB));
  Pull_Resistor pull_resistor_6 (.node(REGS_DATA_MUX));
  Multiplexer #(.width(32)) multiplexer_1 (
    .in0(register_2_q), .in1(INSTR_CONST), .out(VALUE_OUT), .sel(LOAD_CONST_END));
  not not_1 (not_1_out, INSTR_CONST[15]);
  D_Flip_Flop u_FETCH (.D(or_10_out), .clk(CLOCK), .Q(FETCH), .preset(1'b0), .reset(RESET));  // open: Qn
  or or_10 (or_10_out, JUMP, LOAD_RAM_START, LOAD_CONST, START);
  D_Flip_Flop u_LOAD_RAM (.D(LOAD_RAM_START), .clk(CLOCK), .Q(LOAD_RAM), .preset(1'b0), .reset(RESET));  // open: Qn
  and and_1 (LOAD_RAM_START, OPTYPE_DATA, ICODE_0000, START_D1, not_1_out);
  not not_2 (not_2_out, INSTR_CONST[28]);
  not not_3 (not_3_out, INSTR_CONST[29]);
  not not_4 (not_4_out, INSTR_CONST[28]);
  not not_5 (not_5_out, INSTR_CONST[29]);
  nor nor_1 (OPTYPE_DATA, not_2_out, INSTR_CONST[29], INSTR_CONST[30], INSTR_CONST[31]);
  nor nor_2 (OPTYPE_ALU, INSTR_CONST[28], not_3_out, INSTR_CONST[30], INSTR_CONST[31]);
  nor nor_3 (OPTYPE_CTRLFLOW, not_4_out, not_5_out, INSTR_CONST[30], INSTR_CONST[31]);
  D_Flip_Flop LOAD_RAM_END (.D(LOAD_RAM), .clk(CLOCK), .Q(RAM_ADDR_SELECT), .preset(1'b0), .reset(RESET));  // open: Qn
  D_Flip_Flop STEP (.D(or_11_out), .clk(CLOCK), .Q(PC_WRITE), .preset(1'b0), .reset(RESET));  // open: Qn
  or or_11 (or_11_out, JUMP_END, RAM_ADDR_SELECT, LOAD_CONST_END);
  not not_6 (not_6_out, INSTR_CONST[24]);
  not not_7 (not_7_out, INSTR_CONST[25]);
  not not_8 (not_8_out, INSTR_CONST[24]);
  not not_9 (not_9_out, INSTR_CONST[25]);
  nor nor_4 (ICODE_0000, INSTR_CONST[24], INSTR_CONST[25], INSTR_CONST[26], INSTR_CONST[27]);
  nor nor_5 (ICODE_0001, not_6_out, INSTR_CONST[25], INSTR_CONST[26], INSTR_CONST[27]);
  nor nor_6 (ICODE_0010, INSTR_CONST[24], not_7_out, INSTR_CONST[26], INSTR_CONST[27]);
  nor nor_7 (ICODE_0011, not_8_out, not_9_out, INSTR_CONST[26], INSTR_CONST[27]);
  Register #(.width(4)) register_5 (.D(INSTR_CONST[23:20]), .en(START_D1), .clk(CLOCK), .Q(IREG1), .clr(RESET));
  Register #(.width(4)) register_6 (.D(INSTR_CONST[19:16]), .en(START_D1), .clk(CLOCK), .Q(IREG2), .clr(RESET));
  D_Flip_Flop u_LOAD_CONST (.D(and_2_out), .clk(CLOCK), .Q(LOAD_CONST), .preset(1'b0), .reset(RESET));  // open: Qn
  and and_2 (and_2_out, OPTYPE_DATA, ICODE_0000, START_D1, INSTR_CONST[15]);
  D_Flip_Flop u_JUMP (.D(and_3_out), .clk(CLOCK), .Q(JUMP), .preset(1'b0), .reset(RESET));  // open: Qn
  and and_3 (and_3_out, OPTYPE_CTRLFLOW, ICODE_0000, START_D1);
  D_Flip_Flop u_JUMP_END (.D(JUMP), .clk(CLOCK), .Q(JUMP_END), .preset(1'b0), .reset(RESET));  // open: Qn
  D_Flip_Flop u_LOAD_CONST_END (
    .D(LOAD_CONST), .clk(CLOCK), .Q(LOAD_CONST_END), .preset(1'b0), .reset(RESET));  // open: Qn

  // Other names for the same wires on the sheet: CLK = CLOCK; LOAD_RAM_END = RAM_ADDR_SELECT; STEP = PC_WRITE;
  //   VALUE[31:0] = INSTR_CONST; ICONST = INSTR_CONST[15]
endmodule

module REGISTERS_ARRAY (
  input  [31:0] DATA,
  input  [1:0] MODE,
  input  [3:0] SELECT_A,
  input  [3:0] SELECT_B,
  input  CLOCK,
  input  RESET,
  output [31:0] OUT_A,
  output [31:0] OUT_B
);

  wire decoder_1_out0, decoder_1_out1, decoder_1_out2, decoder_1_out3, decoder_3_out0, decoder_3_out1,
       decoder_3_out2, decoder_3_out3, decoder_3_out4, decoder_3_out5, decoder_3_out6, decoder_3_out7,
       decoder_3_out8, decoder_3_out9, decoder_3_out10, decoder_3_out11, decoder_3_out12, decoder_3_out13,
       decoder_3_out14, decoder_3_out15, or_1_out, or_2_out, or_3_out;
  wire [15:0] decoder_2_out0, pull_resistor_1_node;
  wire [31:0] multiplexer_1_out, register32b_1_stored, register32b_2_stored, register32b_3_stored,
       register32b_4_stored, register32b_5_stored, register32b_6_stored, register32b_7_stored,
       register32b_8_stored, register32b_9_stored, register32b_10_stored, register32b_11_stored,
       register32b_12_stored, register32b_13_stored, register32b_14_stored, register32b_15_stored,
       register32b_16_stored;

  or or_1 (or_1_out, decoder_1_out1, decoder_1_out3);
  Decoder #(.select(2)) decoder_1 (
    .out0(decoder_1_out0), .out1(decoder_1_out1), .out2(decoder_1_out2), .out3(decoder_1_out3), .sel(MODE));  // open: en
  or or_2 (or_2_out, decoder_1_out0, decoder_1_out1, decoder_1_out2);
  Decoder #(.select(4)) decoder_2 (
    .out0(decoder_2_out0[0]), .out1(decoder_2_out0[1]), .out2(decoder_2_out0[2]), .out3(decoder_2_out0[3]),
    .out4(decoder_2_out0[4]), .out5(decoder_2_out0[5]), .out6(decoder_2_out0[6]), .out7(decoder_2_out0[7]),
    .out8(decoder_2_out0[8]), .out9(decoder_2_out0[9]), .out10(decoder_2_out0[10]),
    .out11(decoder_2_out0[11]), .out12(decoder_2_out0[12]), .out13(decoder_2_out0[13]),
    .out14(decoder_2_out0[14]), .out15(decoder_2_out0[15]), .sel(SELECT_B), .en(or_1_out));
  Multiplexer #(.width(32)) multiplexer_1 (.in0(OUT_A), .in1(DATA), .out(multiplexer_1_out), .sel(decoder_1_out3));
  or or_3 (or_3_out, decoder_1_out2, decoder_1_out3);
  Pull_Resistor pull_resistor_1 (.node(pull_resistor_1_node));
  assign pull_resistor_1_node = or_3_out ? decoder_2_out0 : 16'bz;  // Controlled_Buffer controlled_buffer_1
  Decoder #(.select(4)) decoder_3 (
    .out0(decoder_3_out0), .out1(decoder_3_out1), .out2(decoder_3_out2), .out3(decoder_3_out3),
    .out4(decoder_3_out4), .out5(decoder_3_out5), .out6(decoder_3_out6), .out7(decoder_3_out7),
    .out8(decoder_3_out8), .out9(decoder_3_out9), .out10(decoder_3_out10), .out11(decoder_3_out11),
    .out12(decoder_3_out12), .out13(decoder_3_out13), .out14(decoder_3_out14), .out15(decoder_3_out15),
    .sel(SELECT_A), .en(or_2_out));
  assign OUT_A = decoder_3_out0 ? register32b_1_stored : 32'bz;  // Controlled_Buffer controlled_buffer_2
  REGISTER32b register32b_1 (
    .DATA(multiplexer_1_out), .WRITE(pull_resistor_1_node[0]), .CLOCK(CLOCK), .RESET(RESET),
    .STORED(register32b_1_stored));
  REGISTER32b register32b_2 (
    .DATA(multiplexer_1_out), .WRITE(pull_resistor_1_node[1]), .CLOCK(CLOCK), .RESET(RESET),
    .STORED(register32b_2_stored));
  REGISTER32b register32b_3 (
    .DATA(multiplexer_1_out), .WRITE(pull_resistor_1_node[2]), .CLOCK(CLOCK), .RESET(RESET),
    .STORED(register32b_3_stored));
  REGISTER32b register32b_4 (
    .DATA(multiplexer_1_out), .WRITE(pull_resistor_1_node[3]), .CLOCK(CLOCK), .RESET(RESET),
    .STORED(register32b_4_stored));
  REGISTER32b register32b_5 (
    .DATA(multiplexer_1_out), .WRITE(pull_resistor_1_node[4]), .CLOCK(CLOCK), .RESET(RESET),
    .STORED(register32b_5_stored));
  REGISTER32b register32b_6 (
    .DATA(multiplexer_1_out), .WRITE(pull_resistor_1_node[5]), .CLOCK(CLOCK), .RESET(RESET),
    .STORED(register32b_6_stored));
  REGISTER32b register32b_7 (
    .DATA(multiplexer_1_out), .WRITE(pull_resistor_1_node[6]), .CLOCK(CLOCK), .RESET(RESET),
    .STORED(register32b_7_stored));
  REGISTER32b register32b_8 (
    .DATA(multiplexer_1_out), .WRITE(pull_resistor_1_node[7]), .CLOCK(CLOCK), .RESET(RESET),
    .STORED(register32b_8_stored));
  REGISTER32b register32b_9 (
    .DATA(multiplexer_1_out), .WRITE(pull_resistor_1_node[8]), .CLOCK(CLOCK), .RESET(RESET),
    .STORED(register32b_9_stored));
  REGISTER32b register32b_10 (
    .DATA(multiplexer_1_out), .WRITE(pull_resistor_1_node[9]), .CLOCK(CLOCK), .RESET(RESET),
    .STORED(register32b_10_stored));
  REGISTER32b register32b_11 (
    .DATA(multiplexer_1_out), .WRITE(pull_resistor_1_node[10]), .CLOCK(CLOCK), .RESET(RESET),
    .STORED(register32b_11_stored));
  REGISTER32b register32b_12 (
    .DATA(multiplexer_1_out), .WRITE(pull_resistor_1_node[11]), .CLOCK(CLOCK), .RESET(RESET),
    .STORED(register32b_12_stored));
  REGISTER32b register32b_13 (
    .DATA(multiplexer_1_out), .WRITE(pull_resistor_1_node[12]), .CLOCK(CLOCK), .RESET(RESET),
    .STORED(register32b_13_stored));
  REGISTER32b register32b_14 (
    .DATA(multiplexer_1_out), .WRITE(pull_resistor_1_node[13]), .CLOCK(CLOCK), .RESET(RESET),
    .STORED(register32b_14_stored));
  REGISTER32b register32b_15 (
    .DATA(multiplexer_1_out), .WRITE(pull_resistor_1_node[14]), .CLOCK(CLOCK), .RESET(RESET),
    .STORED(register32b_15_stored));
  REGISTER32b register32b_16 (
    .DATA(multiplexer_1_out), .WRITE(pull_resistor_1_node[15]), .CLOCK(CLOCK), .RESET(RESET),
    .STORED(register32b_16_stored));
  assign OUT_A = decoder_3_out1 ? register32b_2_stored : 32'bz;  // Controlled_Buffer controlled_buffer_3
  assign OUT_A = decoder_3_out2 ? register32b_3_stored : 32'bz;  // Controlled_Buffer controlled_buffer_4
  assign OUT_A = decoder_3_out3 ? register32b_4_stored : 32'bz;  // Controlled_Buffer controlled_buffer_5
  assign OUT_A = decoder_3_out4 ? register32b_5_stored : 32'bz;  // Controlled_Buffer controlled_buffer_6
  assign OUT_A = decoder_3_out5 ? register32b_6_stored : 32'bz;  // Controlled_Buffer controlled_buffer_7
  assign OUT_A = decoder_3_out6 ? register32b_7_stored : 32'bz;  // Controlled_Buffer controlled_buffer_8
  assign OUT_A = decoder_3_out7 ? register32b_8_stored : 32'bz;  // Controlled_Buffer controlled_buffer_9
  assign OUT_A = decoder_3_out8 ? register32b_9_stored : 32'bz;  // Controlled_Buffer controlled_buffer_10
  assign OUT_A = decoder_3_out9 ? register32b_10_stored : 32'bz;  // Controlled_Buffer controlled_buffer_11
  assign OUT_A = decoder_3_out10 ? register32b_11_stored : 32'bz;  // Controlled_Buffer controlled_buffer_12
  assign OUT_A = decoder_3_out11 ? register32b_12_stored : 32'bz;  // Controlled_Buffer controlled_buffer_13
  assign OUT_A = decoder_3_out12 ? register32b_13_stored : 32'bz;  // Controlled_Buffer controlled_buffer_14
  assign OUT_A = decoder_3_out13 ? register32b_14_stored : 32'bz;  // Controlled_Buffer controlled_buffer_15
  assign OUT_A = decoder_3_out14 ? register32b_15_stored : 32'bz;  // Controlled_Buffer controlled_buffer_16
  assign OUT_A = decoder_3_out15 ? register32b_16_stored : 32'bz;  // Controlled_Buffer controlled_buffer_17
  assign OUT_B = decoder_2_out0[0] ? register32b_1_stored : 32'bz;  // Controlled_Buffer controlled_buffer_18
  assign OUT_B = decoder_2_out0[1] ? register32b_2_stored : 32'bz;  // Controlled_Buffer controlled_buffer_19
  assign OUT_B = decoder_2_out0[2] ? register32b_3_stored : 32'bz;  // Controlled_Buffer controlled_buffer_20
  assign OUT_B = decoder_2_out0[3] ? register32b_4_stored : 32'bz;  // Controlled_Buffer controlled_buffer_21
  assign OUT_B = decoder_2_out0[4] ? register32b_5_stored : 32'bz;  // Controlled_Buffer controlled_buffer_22
  assign OUT_B = decoder_2_out0[5] ? register32b_6_stored : 32'bz;  // Controlled_Buffer controlled_buffer_23
  assign OUT_B = decoder_2_out0[6] ? register32b_7_stored : 32'bz;  // Controlled_Buffer controlled_buffer_24
  assign OUT_B = decoder_2_out0[7] ? register32b_8_stored : 32'bz;  // Controlled_Buffer controlled_buffer_25
  assign OUT_B = decoder_2_out0[8] ? register32b_9_stored : 32'bz;  // Controlled_Buffer controlled_buffer_26
  assign OUT_B = decoder_2_out0[9] ? register32b_10_stored : 32'bz;  // Controlled_Buffer controlled_buffer_27
  assign OUT_B = decoder_2_out0[10] ? register32b_11_stored : 32'bz;  // Controlled_Buffer controlled_buffer_28
  assign OUT_B = decoder_2_out0[11] ? register32b_12_stored : 32'bz;  // Controlled_Buffer controlled_buffer_29
  assign OUT_B = decoder_2_out0[12] ? register32b_13_stored : 32'bz;  // Controlled_Buffer controlled_buffer_30
  assign OUT_B = decoder_2_out0[13] ? register32b_14_stored : 32'bz;  // Controlled_Buffer controlled_buffer_31
  assign OUT_B = decoder_2_out0[14] ? register32b_15_stored : 32'bz;  // Controlled_Buffer controlled_buffer_32
  assign OUT_B = decoder_2_out0[15] ? register32b_16_stored : 32'bz;  // Controlled_Buffer controlled_buffer_33

  // Other names for the same wires on the sheet: CLK = CLOCK
endmodule
